# Fritzing sketch WateringSystem (saved by Fritzing 0.7.11b)
breadboards: 1
perfboards: 1

parts:
  Relay = Arduino Power Driver Shield
  Light_Sensor = Ambient Light Sensor (TEMT6000 Breakout Board)
  RTC = Real Time Clock Module - DS1307 RTC Breakout Board
  Master_Led = LED - 3mm [color="Green (555nm)" package="3 mm [THT]"]
  Master_Switch = Toggle Switch [package=THT]
  Temp = Humidity and Temperature Sensor RHT03
  LED_5 = LED - 3mm [color="Red (633nm)" package="3 mm [THT]"]
  R5 = Resistor [tolerance=±1% resistance=470 package=THT]
  LED_4 = LED - 3mm [color="Red (633nm)" package="3 mm [THT]"]
  LED_3 = LED - 3mm [color="Red (633nm)" package="3 mm [THT]"]
  LED_2 = LED - 3mm [color="Red (633nm)" package="3 mm [THT]"]
  LED_1 = LED - 3mm [color="Red (633nm)" package="3 mm [THT]"]
  R4 = Resistor [tolerance=±1% resistance=470 package=THT]
  R3 = Resistor [tolerance=±1% resistance=470 package=THT]
  R2 = Resistor [tolerance=±1% resistance=470 package=THT]
  R1 = Resistor [tolerance=±1% resistance=470 package=THT]
  Power_12v = Screw terminal - 2 pins [package=THT]
  Power_Plug = Power plug
  Solenoid_1 = Solenoid
  Solenoid_2 = Solenoid
  R6G = Resistor [tolerance=±1% resistance=470 package=THT]
  Arduino1 = Arduino  # not connected

nets:
  N1: Relay.D5-12V, Solenoid_2.pin1
  N2: Relay.12V, Solenoid_1.pin2, Solenoid_2.pin2
  N3: Relay.D3-12V, Solenoid_1.pin1
  5V: Relay.5V_ARDUINO, RTC.5V, Master_Switch.COM, Temp.Vcc
  N4: Relay.A0, Light_Sensor.S
  N5: Relay.A4, RTC.SDA
  N6: Relay.A5, RTC.SCL
  N7: Relay.D2, Temp.Data-signal
  N8: Relay.D5, R1.Pin_0
  N9: Relay.D6, R2.Pin_0
  N10: Relay.D7, R3.Pin_0
  N11: Relay.D8, R4.Pin_0
  N12: Relay.D9, R5.Pin_0
  GND: Relay.GND, Light_Sensor.GND, RTC.GND, Temp.GND_1, LED_5.cathode, LED_4.cathode, LED_3.cathode, LED_2.cathode, LED_1.cathode
  N13: Light_Sensor.VCC, Master_Switch.L2, R6G.Pin_0
  N14: Master_Led.anode, R6G.Pin_1
  N15: LED_5.anode, R5.Pin_1
  N16: LED_4.anode, R4.Pin_1
  N17: LED_3.anode, R3.Pin_1
  N18: LED_2.anode, R2.Pin_1
  N19: LED_1.anode, R1.Pin_1
  N20: Power_12v.pin1, Power_Plug.VCC
  N21: Power_12v.pin2, Power_Plug.GND

notes:
  X5 Seloinds
  Automatic Watering System
  Rain Sensor. Just a plain perf board.
